# Fritzing sketch photoresistorr_read (saved by Fritzing 0.9.4)
breadboards: 1

parts:
  R1 = Resistor [tolerance=±5% resistance=220 package=THT]
  LED1 = LED - 5mm [color="Red (633nm)" package="5 mm [THT]"]
  R2 = Resistor [tolerance=±5% resistance=220 package=THT]
  R3 = Photocell (LDR) [package=THT]
  Part1 = Arduino Uno (Rev3)

nets:
  N1: R1.Pin_0, LED1.cathode, Part1.GND
  N2: R1.Pin_1, R3.pin_0, Part1.A0
  N3: LED1.anode, R2.Pin_0
  N4: R2.Pin_1, Part1.D9_PWM
  N5: R3.pin_1, Part1.3V3
